// Logisim project Kmap-to-circuit.circ as structural Verilog: 1 circuit, main circuit main
module main (
  input  I3_D,
  input  I2_C,
  input  I1_B,
  input  I0_A,
  output O3,
  output O2,
  output O1,
  output O0
);

  wire and_1_out, and_2_out, and_3_out, and_4_out, and_5_out, and_6_out, and_7_out, and_8_out, and_9_out,
       and_10_out, and_11_out, and_12_out, and_13_out, and_14_out, and_15_out, not_1_out, not_2_out,
       not_3_out, not_4_out;

  not not_1 (not_1_out, I2_C);
  not not_2 (not_2_out, I3_D);
  not not_3 (not_3_out, I1_B);
  not not_4 (not_4_out, I0_A);
  and and_1 (and_1_out, not_4_out, I1_B, I3_D);
  and and_2 (and_2_out, I0_A, not_3_out, I3_D);
  and and_3 (and_3_out, I0_A, I1_B, not_1_out);
  and and_4 (and_4_out, not_3_out, not_1_out, I3_D);
  and and_5 (and_5_out, I0_A, I1_B, not_1_out);
  and and_6 (and_6_out, not_4_out, I2_C);
  and and_7 (and_7_out, I1_B, not_2_out);
  and and_8 (and_8_out, not_4_out, not_3_out, not_1_out);
  and and_9 (and_9_out, not_3_out, not_2_out);
  and and_10 (and_10_out, I2_C, not_2_out);
  and and_11 (and_11_out, not_4_out, not_3_out, I3_D);
  and and_12 (and_12_out, I0_A, I1_B, I2_C);
  and and_13 (and_13_out, not_1_out, not_2_out);
  and and_14 (and_14_out, I0_A, not_2_out);
  and and_15 (and_15_out, not_4_out, not_3_out, not_1_out, not_2_out);
  or or_1 (O0, and_15_out, and_1_out, and_2_out, and_3_out);
  or or_2 (O1, and_4_out, and_5_out, and_6_out, and_7_out);
  or or_3 (O2, and_8_out, and_9_out, and_10_out);
  or or_4 (O3, and_11_out, and_12_out, and_13_out, and_14_out);
endmodule
